# Fritzing sketch remoht-arduino (saved by Fritzing 0.7.11b)

parts:
  Part1 = Arduino Pro Mini 3.3V
  T1 = LM35 Temperature Sensor [package="TO92 [THT]"]
  R1 = Photocell (LDR) [package=THT]
  LED1 = LED - 5mm [color="Red (633nm)" package="5 mm [THT]"]
  LED2 = LED - 5mm [color="Red (633nm)" package="5 mm [THT]"]
  J1 = Infrared Proximity Sensor
  Power_plug1 = Power plug
  R2 = 1k Ω Resistor [package=THT]

nets:
  VCC: Part1.VCC, T1.+Vs, R1.pin_1, J1.Vcc, Power_plug1.VCC
  GND: Part1.GND, T1.GND, Power_plug1.GND, R2.Pin_1
  N1: Part1.A1, T1.Vout
  N2: Part1.A0, R1.pin_0, R2.Pin_0
  N3: Part1.D4, J1.Vout
  N4: Part1.D3, LED2.anode
  N5: Part1.D2, LED1.anode
  N6: LED1.cathode, LED2.cathode, J1.GND
